// Logisim project ALU.circ as structural Verilog: 8 circuits, main circuit ALU
module ALU (
  input  [31:0] A,
  input  [31:0] B,
  input  [3:0] OPERATION,
  output [31:0] out,
  output PF,
  output ZF,
  output NF,
  output EQUAL,
  output [31:0] HI
);

  wire and_2_out, comparator_1_lt, comparator_2_lt;
  wire [31:0] add, \and , hi_div, hi_divu, hi_mul, hi_mulu, lo_div, lo_divu, lo_mul, lo_mulu, \nor , \or ,
       S_less, sub, U_less, \xor ;

  MULU mulu_1 (.A(A), .B(B), .LO(lo_mulu), .HI(hi_mulu));
  DIV div_1 (.A(A), .B(B), .LO(lo_div), .HI(hi_div));
  Multiplier #(.width(32)) multiplier_1 (.a(A), .b(B), .out(lo_mul), .cout(hi_mul));  // open: cin
  Divider #(.width(32)) divider_1 (.a(A), .b(B), .out(lo_divu), .rem(hi_divu));  // open: upper
  Adder #(.width(32)) adder_1 (.a(A), .b(B), .out(add));  // open: cin, cout
  Subtractor #(.width(32)) subtractor_1 (.a(A), .b(B), .out(sub));  // open: bin, bout
  Comparator #(.width(32)) comparator_1 (.a(A), .b(B), .eq(EQUAL), .lt(comparator_1_lt));  // open: gt
  assign S_less = {{31{1'b0}}, comparator_1_lt};  // Bit_Extender bit_extender_1
  Comparator #(.width(32)) comparator_2 (.a(A), .b(B), .lt(comparator_2_lt));  // open: gt, eq
  assign U_less = {{31{1'b0}}, comparator_2_lt};  // Bit_Extender bit_extender_2
  assign \and  = A & B;  // AND_Gate and_1, 32 bits wide
  assign \or  = A | B;  // OR_Gate or_1, 32 bits wide
  assign \xor  = A ^ B;  // XOR_Gate xor_1, 32 bits wide
  assign \nor  = ~(A | B);  // NOR_Gate nor_1, 32 bits wide
  Multiplexer #(.select(4), .width(32), .disabled(0), .enable("false")) multiplexer_1 (
    .in0({32{1'b0}}), .in1(A), .in2(S_less), .in3(U_less), .in4(lo_mul), .in5(lo_mulu), .in6(lo_div),
    .in7(lo_divu), .in8(add), .in9(sub), .in10(\and ), .in11(\or ), .in12(\nor ), .in13(\xor ), .out(out),
    .sel(OPERATION));  // open: in14, in15
  Multiplexer #(.select(2), .width(32)) multiplexer_2 (
    .in0(hi_mul), .in1(hi_mulu), .in2(hi_div), .in3(hi_divu), .out(HI), .sel(OPERATION[1:0]), .en(and_2_out));
  Comparator #(.width(32)) comparator_3 (.a(out), .b({32{1'b0}}), .gt(PF), .eq(ZF), .lt(NF));
  and and_2 (and_2_out, OPERATION[2], ~OPERATION[3]);  // AND_Gate

  // Other names for the same wires on the sheet: Op[3:0] = OPERATION

  // Notes on the sheet:
  //   ALU
endmodule

// +X
module MULU (
  input  [31:0] A,
  input  [31:0] B,
  output [31:0] LO,
  output [31:0] HI
);

  wire [31:0] adder_1_out, multiplexer_1_out, multiplexer_2_out, multiplier_1_cout;

  Multiplexer #(.width(32), .enable("false")) multiplexer_1 (
    .in0({32{1'b0}}), .in1(A), .out(multiplexer_1_out), .sel(B[31]));
  Multiplexer #(.width(32), .enable("false")) multiplexer_2 (
    .in0({32{1'b0}}), .in1(B), .out(multiplexer_2_out), .sel(A[31]));
  Multiplier #(.width(32)) multiplier_1 (.a(A), .b(B), .out(LO), .cout(multiplier_1_cout));  // open: cin
  Adder #(.width(32)) adder_1 (.a(multiplexer_1_out), .b(multiplexer_2_out), .out(adder_1_out));  // open: cin, cout
  Adder #(.width(32)) adder_2 (.a(multiplier_1_cout), .b(adder_1_out), .out(HI));  // open: cin, cout

  // Notes on the sheet:
  //   INPUTS
  //   MULU
  //   OUTPUTS
endmodule

module DIV (
  input  [31:0] A,
  input  [31:0] LO,
  input  [31:0] HI,
  input  [31:0] B
);

  wire xor_1_out;
  wire [31:0] divider_1_out, multiplexer_1_out, multiplexer_2_out, negator_1_out, negator_2_out,
       negator_3_out;

  Negator #(.width(32)) negator_1 (.in(A), .out(negator_1_out));
  Negator #(.width(32)) negator_2 (.in(B), .out(negator_2_out));
  Multiplexer #(.width(32), .enable("false")) multiplexer_1 (
    .in0(A), .in1(negator_1_out), .out(multiplexer_1_out), .sel(A[31]));
  Multiplexer #(.width(32), .enable("false")) multiplexer_2 (
    .in0(B), .in1(negator_2_out), .out(multiplexer_2_out), .sel(B[31]));
  Divider #(.width(32)) divider_1 (
    .a(multiplexer_1_out), .b(multiplexer_2_out), .out(divider_1_out), .rem(HI));  // open: upper
  xor xor_1 (xor_1_out, A[31], B[31]);
  Negator #(.width(32)) negator_3 (.in(divider_1_out), .out(negator_3_out));
  Multiplexer #(.width(32), .enable("false")) multiplexer_3 (
    .in0(divider_1_out), .in1(negator_3_out), .out(LO), .sel(xor_1_out));

  // Notes on the sheet:
  //   DIV
endmodule

module REGISTER_FILE (
  input  [31:0] DI,
  input  [31:0] L,
  input  [31:0] H,
  input  [4:0] RD,
  input  [4:0] RS,
  input  [4:0] RT,
  input  CLOCK,
  input  RESET,
  input  LOAD,
  input  SELECT,
  input  POP_PUSH,
  input  INIT_SP,
  input  LOAD_SP,
  input  R_W,
  output [31:0] DRS,
  output [31:0] DRT,
  output [31:0] HI_LO
);

  wire L1, L2, L3, L4, L5, L6, L7, L8, L9, L10, L11, L12, L13, L14, L15, L16, L17, L18, L19, L20, L21, L22,
       L23, L24, L25, L26, L27, L28, L29, L30, LSP, LSP2;
  wire [31:0] adder_1_out, HI, LO, multiplexer_1_out, multiplexer_2_out, N_SP, Q0, Q1, Q2, Q3, Q4, Q5, Q6,
       Q7, Q8, Q9, Q10, Q11, Q12, Q13, Q14, Q15, Q16, Q17, Q18, Q19, Q20, Q21, Q22, Q23, Q24, Q25, Q26, Q27,
       Q28, Q29, Q30, QSP;

  Register #(.width(32)) R0 (.Q(Q0), .clk(CLOCK), .clr(RESET));  // open: D, en
  Register #(.width(32)) R4 (.D(DI), .en(L4), .Q(Q4), .clk(CLOCK), .clr(RESET));
  Register #(.width(32)) R8 (.D(DI), .en(L8), .Q(Q8), .clk(CLOCK), .clr(RESET));
  Register #(.width(32)) R12 (.D(DI), .en(L12), .Q(Q12), .clk(CLOCK), .clr(RESET));
  Register #(.width(32)) R16 (.D(DI), .en(L16), .Q(Q16), .clk(CLOCK), .clr(RESET));
  Register #(.width(32)) R20 (.D(DI), .en(L20), .Q(Q20), .clk(CLOCK), .clr(RESET));
  Register #(.width(32)) R24 (.D(DI), .en(L24), .Q(Q24), .clk(CLOCK), .clr(RESET));
  Register #(.width(32)) R28 (.D(DI), .en(L28), .Q(Q28), .clk(CLOCK), .clr(RESET));
  or or_1 (LSP, LOAD_SP, LSP2);
  Register #(.width(32)) R1 (.D(DI), .en(L1), .Q(Q1), .clk(CLOCK), .clr(RESET));
  Register #(.width(32)) R5 (.D(DI), .en(L5), .Q(Q5), .clk(CLOCK), .clr(RESET));
  Register #(.width(32)) R9 (.D(DI), .en(L9), .Q(Q9), .clk(CLOCK), .clr(RESET));
  Register #(.width(32)) R13 (.D(DI), .en(L13), .Q(Q13), .clk(CLOCK), .clr(RESET));
  Register #(.width(32)) R17 (.D(DI), .en(L17), .Q(Q17), .clk(CLOCK), .clr(RESET));
  Register #(.width(32)) R21 (.D(DI), .en(L21), .Q(Q21), .clk(CLOCK), .clr(RESET));
  Register #(.width(32)) R25 (.D(DI), .en(L25), .Q(Q25), .clk(CLOCK), .clr(RESET));
  Register #(.width(32)) R29 (.D(DI), .en(L29), .Q(Q29), .clk(CLOCK), .clr(RESET));
  Multiplexer #(.width(32)) multiplexer_1 (
    .in0(32'h4), .in1(32'hfffffffc), .out(multiplexer_1_out), .sel(POP_PUSH));  // open: en
  Register #(.width(32)) u_LO (.D(L), .en(LOAD), .Q(LO), .clk(CLOCK), .clr(RESET));
  Adder #(.width(32)) adder_1 (.a(multiplexer_1_out), .b(QSP), .out(adder_1_out));  // open: cin, cout
  Register #(.width(32)) R2 (.D(DI), .en(L2), .Q(Q2), .clk(CLOCK), .clr(RESET));
  Register #(.width(32)) R6 (.D(DI), .en(L6), .Q(Q6), .clk(CLOCK), .clr(RESET));
  Register #(.width(32)) R10 (.D(DI), .en(L10), .Q(Q10), .clk(CLOCK), .clr(RESET));
  Register #(.width(32)) R14 (.D(DI), .en(L14), .Q(Q14), .clk(CLOCK), .clr(RESET));
  Register #(.width(32)) R18 (.D(DI), .en(L18), .Q(Q18), .clk(CLOCK), .clr(RESET));
  Register #(.width(32)) R22 (.D(DI), .en(L22), .Q(Q22), .clk(CLOCK), .clr(RESET));
  Register #(.width(32)) R26 (.D(DI), .en(L26), .Q(Q26), .clk(CLOCK), .clr(RESET));
  Register #(.width(32)) R30 (.D(DI), .en(L30), .Q(Q30), .clk(CLOCK), .clr(RESET));
  Multiplexer #(.width(32)) multiplexer_2 (
    .in0(adder_1_out), .in1(32'h100000), .out(multiplexer_2_out), .sel(INIT_SP));  // open: en
  Multiplexer #(.width(32)) multiplexer_3 (.in0(DI), .in1(multiplexer_2_out), .out(N_SP), .sel(LOAD_SP));  // open: en
  Register #(.width(32)) R3 (.D(DI), .en(L3), .Q(Q3), .clk(CLOCK), .clr(RESET));
  Register #(.width(32)) R7 (.D(DI), .en(L7), .Q(Q7), .clk(CLOCK), .clr(RESET));
  Register #(.width(32)) R11 (.D(DI), .en(L11), .Q(Q11), .clk(CLOCK), .clr(RESET));
  Register #(.width(32)) R15 (.D(DI), .en(L15), .Q(Q15), .clk(CLOCK), .clr(RESET));
  Register #(.width(32)) R19 (.D(DI), .en(L19), .Q(Q19), .clk(CLOCK), .clr(RESET));
  Register #(.width(32)) R23 (.D(DI), .en(L23), .Q(Q23), .clk(CLOCK), .clr(RESET));
  Register #(.width(32)) R27 (.D(DI), .en(L27), .Q(Q27), .clk(CLOCK), .clr(RESET));
  Register #(.width(32)) R31_SP (.D(N_SP), .en(LSP), .Q(QSP), .clk(CLOCK), .clr(RESET));
  Register #(.width(32)) u_HI (.D(H), .en(LOAD), .Q(HI), .clk(CLOCK), .clr(RESET));
  Multiplexer #(.select(5), .width(32)) multiplexer_4 (
    .in0(Q0), .in1(Q1), .in2(Q2), .in3(Q3), .in4(Q4), .in5(Q5), .in6(Q6), .in7(Q7), .in8(Q8), .in9(Q9),
    .in10(Q10), .in11(Q11), .in12(Q12), .in13(Q13), .in14(Q14), .in15(Q15), .in16(Q16), .in17(Q17),
    .in18(Q18), .in19(Q19), .in20(Q20), .in21(Q21), .in22(Q22), .in23(Q23), .in24(Q24), .in25(Q25),
    .in26(Q26), .in27(Q27), .in28(Q28), .in29(Q29), .in30(Q30), .in31(QSP), .out(DRS), .sel(RS));  // open: en
  Multiplexer #(.select(5), .width(32)) multiplexer_5 (
    .in0(Q0), .in1(Q1), .in2(Q2), .in3(Q3), .in4(Q4), .in5(Q5), .in6(Q6), .in7(Q7), .in8(Q8), .in9(Q9),
    .in10(Q10), .in11(Q11), .in12(Q12), .in13(Q13), .in14(Q14), .in15(Q15), .in16(Q16), .in17(Q17),
    .in18(Q18), .in19(Q19), .in20(Q20), .in21(Q21), .in22(Q22), .in23(Q23), .in24(Q24), .in25(Q25),
    .in26(Q26), .in27(Q27), .in28(Q28), .in29(Q29), .in30(Q30), .in31(QSP), .out(DRS), .sel(RT));  // open: en
  Multiplexer #(.width(32)) multiplexer_6 (.in0(HI), .in1(LO), .out(HI_LO), .sel(SELECT));  // open: en
  Demultiplexer #(.select(5)) demultiplexer_1 (
    .out1(L1), .out2(L2), .out3(L3), .out4(L4), .out5(L5), .out6(L6), .out7(L7), .out8(L8), .out9(L9),
    .out10(L10), .out11(L11), .out12(L12), .out13(L13), .out14(L14), .out15(L15), .out16(L16), .out17(L17),
    .out18(L18), .out19(L19), .out20(L20), .out21(L21), .out22(L22), .out23(L23), .out24(L24), .out25(L25),
    .out26(L26), .out27(L27), .out28(L28), .out29(L29), .out30(L30), .out31(LSP2), .in(R_W), .sel(RD));  // open: out0, en

  // Other names for the same wires on the sheet: CLK = CLOCK; I_SP = INIT_SP; LM_D = LOAD; LSP1 = LOAD_SP;
  //   RST = RESET; SELECTOR_H_L = SELECT

  // Notes on the sheet:
  //   INPUTS
  //   DATA IN
  //   LOW AND HIGH
  //   DATA ADRRESS
  //   SELECTOR A
  //   SELECTOR B
  //   CLOCK
  //   RESET
  //   READ/WRITE
  //   REGISTER FILE
  //   OUTPUTS
endmodule

module INSTRUCTION_DECODER (
  input  [31:0] Intruction,
  output [31:0] Constant,
  output [25:0] Jump,
  output [3:0] Unit_Op,
  output [3:0] ALU_Op,
  output [2:0] Branch_Op,
  output [1:0] Special_Op,
  output [4:0] S_A,
  output [4:0] S_B,
  output [4:0] DA,
  output Move_Lo_Hi,
  output pop_push,
  output load_store,
  output Write_RF
);

  wire add, addi, \and , and_1_out, and_32_out, and_33_out, andi, beq, bgtz, blez, bltz, bne, div, divu,
       halt, j, jr, kbd, lw, mflo, mult, mulu, nop, \nor , \or , or_1_out, or_2_out, or_3_out, or_4_out,
       or_5_out, or_6_out, or_7_out, or_8_out, or_9_out, or_10_out, or_11_out, or_12_out, or_13_out,
       or_14_out, or_15_out, or_16_out, or_17_out, ori, pop, rnd, slt, slti, sltiu, sltu, sub, tty, \xor ,
       xori;
  wire [1:0] or_18_out, or_22_out;
  wire [15:0] bit_extender_1_out;

  assign bit_extender_1_out = {{15{Intruction[15]}}, Intruction[15]};  // Bit_Extender bit_extender_1
  or or_1 (or_1_out, andi, xori, ori);
  Multiplexer #(.width(16), .enable("false")) multiplexer_1 (
    .in0(bit_extender_1_out), .in1({16{1'b0}}), .out(Constant[31:16]), .sel(or_1_out));
  or or_2 (or_2_out, mult, mulu, div, divu);
  or or_3 (or_3_out, mflo, Move_Lo_Hi);
  or or_4 (or_4_out, add, \nor , sub, \xor , \and , slt, \or , sltu);
  or or_5 (or_5_out, addi, slti, andi, ori, sltiu, xori);
  or or_6 (or_6_out, pop, pop_push);
  or or_7 (or_7_out, beq, bltz, bne, j, blez, jr, bgtz);
  or or_8 (or_8_out, lw, load_store);
  or or_9 (or_9_out, halt, tty, rnd, kbd);
  Priority_Encoder #(.select(4)) priority_encoder_1 (
    .in0(nop), .in1(or_4_out), .in2(or_5_out), .in3(or_2_out), .in4(or_3_out), .in5(or_6_out),
    .in6(or_7_out), .in7(or_8_out), .in8(or_9_out), .out(Unit_Op));  // open: in9, in10, in11, in12, in13, in14, in15, gs, en_out, en_in
  and and_1 (and_1_out, ~Intruction[26], ~Intruction[27], ~Intruction[28], ~Intruction[29], ~Intruction[30], ~Intruction[31]);  // AND_Gate
  or or_10 (or_10_out, sltu, sltiu);
  or or_11 (or_11_out, lw, add, addi, load_store);
  or or_12 (or_12_out, \and , andi);
  or or_13 (or_13_out, \or , ori);
  and and_2 (add, ~Intruction[0], ~Intruction[1], ~Intruction[2], and_1_out, ~Intruction[3], ~Intruction[4], Intruction[5]);  // AND_Gate
  and and_3 (sub, ~Intruction[0], Intruction[1], ~Intruction[2], and_1_out, ~Intruction[3], ~Intruction[4], Intruction[5]);  // AND_Gate
  and and_4 (mult, ~Intruction[0], ~Intruction[1], ~Intruction[2], and_1_out, Intruction[3], Intruction[4], ~Intruction[5]);  // AND_Gate
  and and_5 (mulu, Intruction[0], ~Intruction[1], ~Intruction[2], and_1_out, Intruction[3], Intruction[4], ~Intruction[5]);  // AND_Gate
  and and_6 (div, ~Intruction[0], Intruction[1], ~Intruction[2], and_1_out, Intruction[3], Intruction[4], ~Intruction[5]);  // AND_Gate
  and and_7 (divu, Intruction[0], Intruction[1], ~Intruction[2], and_1_out, Intruction[3], Intruction[4], ~Intruction[5]);  // AND_Gate
  or or_14 (or_14_out, blez, bgtz, bltz);
  or or_15 (or_15_out, slt, slti);
  or or_16 (or_16_out, \xor , xori);
  Priority_Encoder #(.select(4)) priority_encoder_2 (
    .in0(1'b1), .in1(or_14_out), .in2(or_15_out), .in3(or_10_out), .in4(mult), .in5(mulu), .in6(div),
    .in7(divu), .in8(or_11_out), .in9(sub), .in10(or_12_out), .in11(or_13_out), .in12(\nor ),
    .in13(or_16_out), .out(ALU_Op));  // open: in14, in15, gs, en_out, en_in
  and and_8 (\and , ~Intruction[0], ~Intruction[1], Intruction[2], and_1_out, ~Intruction[3], ~Intruction[4], Intruction[5]);  // AND_Gate
  and and_9 (\or , Intruction[0], ~Intruction[1], Intruction[2], and_1_out, ~Intruction[3], ~Intruction[4], Intruction[5]);  // AND_Gate
  and and_10 (\nor , Intruction[0], Intruction[1], Intruction[2], and_1_out, ~Intruction[3], ~Intruction[4], Intruction[5]);  // AND_Gate
  and and_11 (\xor , ~Intruction[0], ~Intruction[1], ~Intruction[2], and_1_out, Intruction[3], ~Intruction[4], Intruction[5]);  // AND_Gate
  and and_12 (slt, ~Intruction[0], Intruction[1], ~Intruction[2], and_1_out, Intruction[3], ~Intruction[4], Intruction[5]);  // AND_Gate
  and and_13 (sltu, Intruction[0], Intruction[1], ~Intruction[2], and_1_out, Intruction[3], ~Intruction[4], Intruction[5]);  // AND_Gate
  Priority_Encoder #(.disabled(0)) priority_encoder_3 (
    .in0(1'b1), .in1(bne), .in2(blez), .in3(bgtz), .in4(bltz), .in5(j), .in6(jr), .in7(beq), .out(Branch_Op));  // open: en_in, gs, en_out
  or or_17 (or_17_out, add, sltu, sub, slti, mult, sltiu, mulu, beq, div, bne, divu, blez, addi, bgtz, bltz, \or , jr, \nor , lw, \xor , load_store, andi, pop_push, ori, tty, xori, \and , slt);
  and and_14 (Move_Lo_Hi, ~Intruction[0], ~Intruction[1], ~Intruction[2], and_1_out, ~Intruction[3], Intruction[4], ~Intruction[5]);  // AND_Gate
  and and_15 (mflo, ~Intruction[0], Intruction[1], ~Intruction[2], and_1_out, ~Intruction[3], Intruction[4], ~Intruction[5]);  // AND_Gate
  and and_16 (nop, ~Intruction[0], ~Intruction[1], ~Intruction[2], and_1_out, ~Intruction[3], ~Intruction[4], ~Intruction[5]);  // AND_Gate
  and and_17 (jr, ~Intruction[0], ~Intruction[1], ~Intruction[2], and_1_out, Intruction[3], ~Intruction[4], ~Intruction[5]);  // AND_Gate
  and and_18 (lw, Intruction[26], Intruction[27], ~Intruction[28], ~Intruction[29], ~Intruction[30], Intruction[31]);  // AND_Gate
  and and_19 (load_store, Intruction[26], Intruction[27], ~Intruction[28], Intruction[29], ~Intruction[30], Intruction[31]);  // AND_Gate
  Multiplexer #(.width(5), .enable("false")) multiplexer_2 (
    .in0({5{1'b0}}), .in1(Intruction[25:21]), .out(S_A), .sel(or_17_out));
  and and_20 (addi, ~Intruction[26], ~Intruction[27], ~Intruction[28], Intruction[29], ~Intruction[30], ~Intruction[31]);  // AND_Gate
  and and_21 (andi, ~Intruction[26], ~Intruction[27], Intruction[28], Intruction[29], ~Intruction[30], ~Intruction[31]);  // AND_Gate
  and and_22 (ori, Intruction[26], ~Intruction[27], Intruction[28], Intruction[29], ~Intruction[30], ~Intruction[31]);  // AND_Gate
  and and_23 (xori, ~Intruction[26], Intruction[27], Intruction[28], Intruction[29], ~Intruction[30], ~Intruction[31]);  // AND_Gate
  and and_24 (slti, ~Intruction[26], Intruction[27], ~Intruction[28], Intruction[29], ~Intruction[30], ~Intruction[31]);  // AND_Gate
  and and_25 (sltiu, Intruction[26], Intruction[27], ~Intruction[28], Intruction[29], ~Intruction[30], ~Intruction[31]);  // AND_Gate
  or or_18 (or_18_out[0], add, \nor , sub, \xor , mult, slt, mulu, sltu, div, beq, divu, bne, \and , load_store, \or );
  or or_19 (Special_Op[0], rnd, kbd);
  or or_20 (Special_Op[1], kbd, tty);
  Multiplexer #(.select(2), .width(5)) multiplexer_3 (
    .in0({5{1'b0}}), .in1(Intruction[20:16]), .in2({5{1'b1}}), .out(S_B), .sel(or_18_out));  // open: in3, en
  or or_21 (or_18_out[1], pop, pop_push);
  and and_26 (beq, ~Intruction[26], ~Intruction[27], Intruction[28], ~Intruction[29], ~Intruction[30], ~Intruction[31]);  // AND_Gate
  and and_27 (bne, Intruction[26], ~Intruction[27], Intruction[28], ~Intruction[29], ~Intruction[30], ~Intruction[31]);  // AND_Gate
  and and_28 (blez, ~Intruction[26], Intruction[27], Intruction[28], ~Intruction[29], ~Intruction[30], ~Intruction[31]);  // AND_Gate
  and and_29 (bgtz, Intruction[26], Intruction[27], Intruction[28], ~Intruction[29], ~Intruction[30], ~Intruction[31]);  // AND_Gate
  and and_30 (bltz, Intruction[26], ~Intruction[27], ~Intruction[28], ~Intruction[29], ~Intruction[30], ~Intruction[31]);  // AND_Gate
  and and_31 (j, ~Intruction[26], Intruction[27], ~Intruction[28], ~Intruction[29], ~Intruction[30], ~Intruction[31]);  // AND_Gate
  or or_22 (or_22_out[0], add, slt, sub, sltu, \and , Move_Lo_Hi, \or , mflo, \nor , pop, \xor , kbd, rnd);
  or or_23 (or_22_out[1], addi, slti, andi, sltiu, ori, lw, xori);
  and and_32 (and_32_out, ~Intruction[26], ~Intruction[27], ~Intruction[28], Intruction[29], Intruction[30], Intruction[31]);  // AND_Gate
  and and_33 (and_33_out, Intruction[26], Intruction[27], Intruction[28], Intruction[29], Intruction[30], Intruction[31]);
  Multiplexer #(.select(2), .width(5)) multiplexer_4 (
    .in0({5{1'b0}}), .in1(Intruction[15:11]), .in2(Intruction[20:16]), .out(DA), .sel(or_22_out));  // open: in3, en
  and and_34 (pop, ~Intruction[0], ~Intruction[1], ~Intruction[2], and_32_out, ~Intruction[3], ~Intruction[4], ~Intruction[5]);  // AND_Gate
  and and_35 (pop_push, Intruction[0], ~Intruction[1], ~Intruction[2], and_32_out, ~Intruction[3], ~Intruction[4], ~Intruction[5]);  // AND_Gate
  and and_36 (halt, Intruction[0], Intruction[1], Intruction[2], and_33_out, Intruction[3], Intruction[4], Intruction[5]);
  and and_37 (tty, Intruction[0], ~Intruction[1], ~Intruction[2], and_33_out, ~Intruction[3], ~Intruction[4], ~Intruction[5]);  // AND_Gate
  and and_38 (rnd, ~Intruction[0], Intruction[1], ~Intruction[2], and_33_out, ~Intruction[3], ~Intruction[4], ~Intruction[5]);  // AND_Gate
  and and_39 (kbd, ~Intruction[0], ~Intruction[1], Intruction[2], and_33_out, ~Intruction[3], ~Intruction[4], ~Intruction[5]);  // AND_Gate
  or or_24 (Write_RF, add, \xor , sub, slt, \and , sltu, \or , slti, \nor , sltiu, addi, pop, andi, lw, ori, rnd, xori, kbd, Move_Lo_Hi, mflo);

  assign Constant[15:0] = Intruction[15:0];
  assign Jump = Intruction[25:0];

  // Other names for the same wires on the sheet: Cons_Ext[31:0] = {Constant[31:16], Intruction[15:0]};
  //   Constant_t[15:0] = Intruction[15:0]; Destiny_Jump[25:0] = Intruction[25:0]; F1 = Intruction[0];
  //   Func_Code[5:0] = Intruction[5:0]; F2 = Intruction[1]; F3 = Intruction[2]; F4 = Intruction[3];
  //   F5 = Intruction[4]; F6 = Intruction[5]; Rd[4:0] = Intruction[15:11]; Rt[4:0] = Intruction[20:16];
  //   Rs[4:0] = Intruction[25:21]; O1 = Intruction[26]; Op_Code[5:0] = Intruction[31:26]; O2 = Intruction[27];
  //   O3 = Intruction[28]; O4 = Intruction[29]; O5 = Intruction[30]; O6 = Intruction[31]; Lo_Hi = Move_Lo_Hi;
  //   mfhi = Move_Lo_Hi; push = pop_push; sw = load_store; W_RF = Write_RF

  // Notes on the sheet:
  //   Inputs
  //   Ctrl Unit Operation
  //   ALU Operation
  //   INSTRUCTION DECODER
  //   Branch Operation
  //   Selector A
  //   Selector B
  //   Special Operation
  //   Selector DA
  //   Write RF
  //   Outputs
endmodule

module CONTROL_UNIT (
  input  [1:0] Special_Op,
  input  [3:0] Operation,
  input  [3:0] Write_Time,
  input  Reset,
  input  Clock,
  input  End_Hit0,
  input  pop_push,
  input  can_t_pop,
  input  L_S_Ram,
  output [2:0] S_Data,
  output Chip_Select,
  output RI,
  output NI,
  output PC_Eneable,
  output Init_SP,
  output Load_SP,
  output Kbd_Enable,
  output Kbd_Clear,
  output TTY_Enable,
  output STOP,
  output R_W_Ram
);

  wire Again1, Again2, Again3, Again4, Again5, Again6, Again7, Again8, Again9, Again10, Again11, Again12,
       Again13, c_prime_t_push, comparator_1_eq, CS2, CS3, CS4, CS5, d_ff_2_q, d_ff_3_q, d_ff_9_q,
       demultiplexer_1_out0, demultiplexer_1_out1, demultiplexer_2_out0, demultiplexer_3_out1,
       demultiplexer_3_out2, demultiplexer_3_out3, demultiplexer_3_out5, demultiplexer_3_out7,
       demultiplexer_3_out8, demultiplexer_4_out0, demultiplexer_4_out1, demultiplexer_5_out0,
       demultiplexer_7_out0, demultiplexer_7_out1, demultiplexer_8_out0, demultiplexer_9_out0,
       demultiplexer_10_out0, demultiplexer_11_out1, demultiplexer_12_out1, L_SP2, or_3_out, or_4_out,
       or_7_out, or_10_out, or_11_out, or_12_out, or_13_out, SD3, SD3_1, Start, Writed;
  wire [3:0] counter_1_q, subtractor_1_out;

  not not_1 (Start, Reset);
  D_Flip_Flop IDLE (.clk(Clock), .D(demultiplexer_1_out0), .Q(Init_SP), .preset(Reset));  // open: Qn, en, reset
  or or_1 (Chip_Select, RI, CS2, CS3, CS4, CS5);
  or or_2 (PC_Eneable, Again1, Again2, Again3, Again4, Again5, Again6, Again7, Again8, Again9, Again10, Again11, Again12, Again13);
  or or_3 (or_3_out, Init_SP, PC_Eneable);
  Demultiplexer #(.enable("false")) demultiplexer_1 (
    .out0(demultiplexer_1_out0), .out1(demultiplexer_1_out1), .in(or_3_out), .sel(Start));
  or or_4 (or_4_out, demultiplexer_2_out0, demultiplexer_1_out1);
  or or_5 (Load_SP, Init_SP, Again5, L_SP2);
  Priority_Encoder priority_encoder_1 (
    .in0(Again2), .in1(Again3), .in2(SD3), .in3(Again11), .in4(Again13), .out(S_Data));  // open: in5, in6, in7, en_in, gs, en_out
  D_Flip_Flop d_ff_1 (.clk(Clock), .D(or_4_out), .Q(RI), .reset(Reset));  // open: Qn, preset, en
  Demultiplexer demultiplexer_2 (.out0(demultiplexer_2_out0), .out1(NI), .in(RI), .sel(End_Hit0));  // open: en
  or or_6 (SD3, SD3_1, Again9);
  or or_7 (or_7_out, CS3, CS5);
  Subtractor #(.width(4)) subtractor_1 (.a(Write_Time), .b(4'b0001), .out(subtractor_1_out));  // open: bin, bout
  D_Flip_Flop d_ff_2 (.clk(Clock), .D(or_7_out), .Q(d_ff_2_q), .reset(Reset));  // open: Qn, preset, en
  D_Flip_Flop d_ff_3 (.clk(Clock), .D(NI), .Q(d_ff_3_q), .reset(Reset));  // open: Qn, preset, en
  or or_8 (R_W_Ram, CS3, CS5);
  Counter #(.width(4), .max('hf)) counter_1 (
    .load(or_7_out), .D(subtractor_1_out), .count(d_ff_2_q), .Q(counter_1_q), .clk(Clock), .clr(Reset));  // open: carry
  Comparator #(.width(4), .mode("unsigned")) comparator_1 (
    .a(counter_1_q), .b(4'b0000), .eq(comparator_1_eq));  // open: gt, lt
  Demultiplexer #(.select(4)) demultiplexer_3 (
    .out0(Again1), .out1(demultiplexer_3_out1), .out2(demultiplexer_3_out2), .out3(demultiplexer_3_out3),
    .out4(Again3), .out5(demultiplexer_3_out5), .out6(Again8), .out7(demultiplexer_3_out7),
    .out8(demultiplexer_3_out8), .in(d_ff_3_q), .sel(Operation));  // open: out9, out10, out11, out12, out13, out14, out15, en
  nand nand_1 (Writed, comparator_1_eq, d_ff_2_q);
  or or_9 (Again2, demultiplexer_3_out1, demultiplexer_3_out2, demultiplexer_3_out3);
  Demultiplexer demultiplexer_4 (
    .out0(demultiplexer_4_out0), .out1(demultiplexer_4_out1), .in(demultiplexer_3_out5), .sel(pop_push));  // open: en
  Demultiplexer demultiplexer_5 (
    .out0(demultiplexer_5_out0), .out1(Again4), .in(demultiplexer_4_out0), .sel(can_t_pop));  // open: en
  Demultiplexer demultiplexer_6 (
    .out0(L_SP2), .out1(Again6), .in(demultiplexer_4_out1), .sel(c_prime_t_push));  // open: en
  Demultiplexer demultiplexer_7 (
    .out0(demultiplexer_7_out0), .out1(demultiplexer_7_out1), .in(demultiplexer_3_out7), .sel(L_S_Ram));  // open: en
  Demultiplexer #(.select(2)) demultiplexer_8 (
    .out0(demultiplexer_8_out0), .out1(Again11), .out2(Again12), .out3(Again13), .in(demultiplexer_3_out8),
    .sel(Special_Op));  // open: en
  D_Flip_Flop d_ff_4 (.clk(Clock), .D(or_10_out), .Q(CS2), .reset(Reset));  // open: Qn, preset, en
  or or_10 (or_10_out, demultiplexer_9_out0, demultiplexer_5_out0);
  or or_11 (or_11_out, L_SP2, demultiplexer_11_out1);
  or or_12 (or_12_out, demultiplexer_10_out0, demultiplexer_7_out0);
  or or_13 (or_13_out, demultiplexer_7_out1, demultiplexer_12_out1);
  Demultiplexer demultiplexer_9 (.out0(demultiplexer_9_out0), .out1(SD3_1), .in(CS2), .sel(End_Hit0));  // open: en
  D_Flip_Flop d_ff_5 (.clk(Clock), .D(or_11_out), .Q(CS3), .reset(Reset));  // open: Qn, preset, en
  Demultiplexer demultiplexer_10 (.out0(demultiplexer_10_out0), .out1(Again9), .in(CS4), .sel(End_Hit0));  // open: en
  D_Flip_Flop d_ff_6 (.clk(Clock), .D(or_12_out), .Q(CS4), .reset(Reset));  // open: Qn, preset, en
  D_Flip_Flop d_ff_7 (.clk(Clock), .D(or_13_out), .Q(CS5), .reset(Reset));  // open: Qn, preset, en
  Demultiplexer demultiplexer_11 (.out0(Again7), .out1(demultiplexer_11_out1), .in(CS3), .sel(Writed));  // open: en
  Demultiplexer demultiplexer_12 (.out0(Again10), .out1(demultiplexer_12_out1), .in(CS5), .sel(Writed));  // open: en
  or or_14 (Kbd_Clear, demultiplexer_8_out0, d_ff_9_q);
  D_Flip_Flop d_ff_8 (.clk(Clock), .D(SD3_1), .Q(Again5), .reset(Reset));  // open: Qn, preset, en
  D_Flip_Flop d_ff_9 (.clk(Clock), .D(Kbd_Clear), .Q(d_ff_9_q), .reset(Reset));  // open: Qn, preset, en

  assign STOP = Kbd_Clear;

  // Other names for the same wires on the sheet: c_prime_t_pop = can_t_pop; Clk = Clock; CS = Chip_Select; CS1 = RI;
  //   End_Hit = End_Hit0; KBD_CLR = Kbd_Clear; L_SP = Load_SP; I_SP = Init_SP; L_SP1 = Init_SP; L_SP3 = Again5;
  //   Load_Store = L_S_Ram; Op[3:0] = Operation; p_p = pop_push; Again = PC_Eneable; PC_E = PC_Eneable;
  //   R_W_Ram1 = CS3; R_W_Ram2 = CS5; S_O[1:0] = Special_Op; SD1 = Again2; SD2 = Again3; SD3_2 = Again9;
  //   SD4 = Again11; KBD_ENABLE_t = Again13; SD5 = Again13; TTY_ENABLE_t = Again12; WT[3:0] = Write_Time

  // Notes on the sheet:
  //   Inputs
  //   CONTROL UNIT
endmodule

module BRANCH_CONTROL (
  input  [31:0] PC,
  input  [31:0] Const,
  input  [25:0] Destiny,
  input  [31:0] A,
  input  N,
  input  Z,
  input  P,
  input  Equal,
  input  [2:0] B_Op,
  output [31:0] PC_out
);

  wire or_1_out;
  wire [31:0] beq, bgtz, blez, bltz, bne, Const_Ext, Jump, Standar;

  Shifter #(.width(32)) shifter_1 (.in(Const), .\dist (5'b00010), .out(Const_Ext));
  or or_1 (or_1_out, N, Z);
  Multiplexer #(.width(32)) multiplexer_1 (.in0(Standar), .in1(Jump), .out(beq), .sel(Equal));  // open: en
  Multiplexer #(.width(32)) multiplexer_2 (.in0(Standar), .in1(Jump), .out(blez), .sel(or_1_out));  // open: en
  Adder #(.width(32)) adder_1 (.a(PC), .b(32'h4), .out(Standar));  // open: cin, cout
  Multiplexer #(.width(32)) multiplexer_3 (.in0(Jump), .in1(Standar), .out(bne), .sel(Equal));  // open: en
  Multiplexer #(.width(32)) multiplexer_4 (.in0(Standar), .in1(Jump), .out(bgtz), .sel(P));  // open: en
  Multiplexer #(.select(3), .width(32)) multiplexer_5 (
    .in0(Standar), .in1(bne), .in2(blez), .in3(bgtz), .in4(bltz), .in5({PC[31:28], Destiny, 2'b00}), .in6(A),
    .in7(beq), .out(PC_out), .sel(B_Op));  // open: en
  Adder #(.width(32)) adder_2 (.a(Const_Ext), .b(Standar), .out(Jump));  // open: cin, cout
  Multiplexer #(.width(32)) multiplexer_6 (.in0(Standar), .in1(Jump), .out(bltz), .sel(N));  // open: en

  // Other names for the same wires on the sheet: J[31:2] = {PC[31:28], Destiny}

  // Notes on the sheet:
  //   B_Op: pull=down
  //   N: pull=down
  //   Z: pull=down
  //   Inputs
  //   BRANCH CONTROL
  //   Outputs
endmodule

module DATA_PATH (
  input  [31:0] IN0,
  input  [31:0] IN1,
  input  [31:0] IN2,
  input  [31:0] IN3,
  input  Reset,
  input  Clk,
  input  [2:0] S_Data,
  input  Init_SP,
  input  Load_SP,
  input  ReadInst,
  input  NewInst,
  input  PC_Enable,
  input  Find,
  input  Kbd_Available,
  input  [6:0] Kbd_ASCII_Data,
  input  R_W_Ram,
  output [31:0] Ou0,
  output [31:0] Ou1,
  output [31:0] Ou2,
  output [31:0] Ou3,
  output [15:0] Ram_Address,
  output [3:0] Mask,
  output [6:0] TTY_ASCII_Data,
  output [3:0] Unit_Op,
  output [1:0] Special_Op,
  output pop_push,
  output L_S_Ram
);

  wire and_2_out, and_3_out, c_prime_t_pop, c_prime_t_push, E, H_L, Input_B, L_H_L, N, P, R_W_RF, Z;
  wire [1:0] OffSet;
  wire [2:0] B_Op;
  wire [3:0] A_Op;
  wire [4:0] DataAddress, Selector_A, Selector_B;
  wire [25:0] Jump;
  wire [31:0] Addr, B, bit_extender_1_out, Cnst, Data_In, Hi, Hi_Lo, Instruction, InstSave, Kybd, Lo,
       multiplexer_1_out, multiplexer_2_out, multiplexer_3_out, multiplexer_5_out, PC, PC_new, Rand;
  wire [31:7] A;

  Multiplexer #(.width(32)) multiplexer_1 (.in0(B), .in1(Cnst), .out(multiplexer_1_out), .sel(Input_B));  // open: en
  REGISTER_FILE register_file_1 (
    .DI(Data_In), .L(Lo), .H(Hi), .RD(DataAddress), .RS(Selector_A), .RT(Selector_B), .CLOCK(Clk),
    .RESET(Reset), .LOAD(Init_SP), .SELECT(L_H_L), .POP_PUSH(H_L), .INIT_SP(pop_push), .LOAD_SP(Load_SP),
    .R_W(R_W_RF), .DRS({A, TTY_ASCII_Data}), .DRT(B), .HI_LO(Hi_Lo));
  ALU alu_1 (
    .A({A, TTY_ASCII_Data}), .B(multiplexer_1_out), .OPERATION(A_Op), .PF(P), .ZF(Z), .NF(N), .EQUAL(E),
    .HI(Hi), .out(Lo));
  and and_1 (L_H_L, Unit_Op[0], Unit_Op[1], ~Unit_Op[2], ~Unit_Op[3]);  // AND_Gate
  and and_2 (and_2_out, ~Unit_Op[0], Unit_Op[1], ~Unit_Op[2], ~Unit_Op[3]);  // AND_Gate
  and and_3 (and_3_out, Unit_Op[0], Unit_Op[1], Unit_Op[2], ~Unit_Op[3]);  // AND_Gate
  or or_1 (Input_B, and_2_out, and_3_out);
  INSTRUCTION_DECODER instruction_decoder_1 (
    .Constant(Cnst), .Jump(Jump), .Unit_Op(Unit_Op), .ALU_Op(A_Op), .Branch_Op(B_Op),
    .Special_Op(Special_Op), .S_A(Selector_A), .S_B(Selector_B), .DA(DataAddress), .Move_Lo_Hi(R_W_RF),
    .pop_push(H_L), .load_store(pop_push), .Write_RF(L_S_Ram), .Intruction(InstSave));
  BRANCH_CONTROL branch_control_1 (
    .PC(PC), .Const(Cnst), .Destiny(Jump), .A({A, TTY_ASCII_Data}), .N(N), .Z(Z), .P(P), .Equal(E),
    .B_Op(B_Op), .PC_out(PC_new));
  Register #(.width(32)) u_Instruction (.D(Instruction), .en(NewInst), .Q(InstSave), .clk(Clk), .clr(Reset));
  Random #(.width(32), .seed(8)) Random (.clk(Clk), .out(Rand), .clr(Reset));  // open: next
  Multiplexer #(.width(32)) multiplexer_2 (.in1(B), .out(multiplexer_2_out), .sel(L_S_Ram));  // open: in0, en
  Multiplexer #(.width(32)) multiplexer_3 (
    .in0(multiplexer_2_out), .in1({A, TTY_ASCII_Data}), .out(multiplexer_3_out), .sel(pop_push));  // open: en
  Multiplexer #(.select(3), .width(32)) multiplexer_4 (
    .in0(Lo), .in1(Hi_Lo), .in2(Instruction), .in3(Rand), .in4(Kybd), .out(Data_In), .sel(S_Data));  // open: in5, in6, in7, en
  Multiplexer #(.width(32)) multiplexer_5 (.in0(B), .in1(Lo), .out(multiplexer_5_out), .sel(Unit_Op[1]));  // open: en
  assign bit_extender_1_out = {{25{1'b0}}, Kbd_ASCII_Data};  // Bit_Extender bit_extender_1
  Demultiplexer #(.select(2), .width(32)) demultiplexer_1 (
    .out0(Ou0), .out1(Ou1), .out2(Ou2), .out3(Ou3),
    .in({multiplexer_3_out[7:0], multiplexer_3_out[15:8], multiplexer_3_out[23:16], multiplexer_3_out[31:24]}),
    .sel(OffSet));  // open: en
  Register #(.width(32)) u_PC (.D(PC_new), .en(PC_Enable), .Q(PC), .clk(Clk), .clr(Reset));
  Multiplexer #(.width(32)) multiplexer_6 (.in0(multiplexer_5_out), .in1(PC), .out(Addr), .sel(ReadInst));  // open: en
  Multiplexer #(.width(32)) multiplexer_7 (
    .in0({32{1'b1}}), .in1(bit_extender_1_out), .out(Kybd), .sel(Kbd_Available));  // open: en
  Comparator #(.width(32)) comparator_1 (.a(Addr), .b(32'h100000), .eq(c_prime_t_pop));  // open: gt, lt
  Comparator #(.width(32)) comparator_2 (.a(Addr), .b(32'h1000), .eq(c_prime_t_push));  // open: gt, lt

  // Other names for the same wires on the sheet: A[6:0] = TTY_ASCII_Data; TTY_DATA[6:0] = TTY_ASCII_Data; F = Find;
  //   I_SP = Init_SP; KBD_AVAIL = Kbd_Available; KBD_DATA[6:0] = Kbd_ASCII_Data; L_SP = Load_SP; Load_Store = L_S_Ram;
  //   NI = NewInst; P_P = pop_push; Ram_addr[15:0] = Ram_Address; RI = ReadInst; UO0 = Unit_Op[0]; UO1 = Unit_Op[1];
  //   UO2 = Unit_Op[2]; UO3 = Unit_Op[3]

  // Notes on the sheet:
  //   Inputs
  //   DATA PATH
  //   Outputs
endmodule
